// Logisim project lr1.circ as structural Verilog
module main (
  input  v,
  input  [2:0] in_2,
  input  x0,
  input  x1,
  input  x2,
  output q0,
  output q1,
  output q2,
  output q3,
  output q4,
  output q5,
  output q6,
  output q7
);

  Decoder #(.select(3)) decoder_1 (
    .out0(q0), .out1(q1), .out2(q2), .out3(q3), .out4(q4), .out5(q5), .out6(q6), .out7(q7), .sel(in_2), .en(v));

  assign x0 = in_2[0];
  assign x1 = in_2[1];
  assign x2 = in_2[2];
endmodule
