// Logisim project lr2.circ as structural Verilog: 6 circuits, main circuit main
module main (
  input  [7:0] in_1,
  input  [7:0] in_2,
  input  [7:0] in_3,
  input  [7:0] in_4,
  input  [1:0] in_5,
  input  in_6,
  output out_7,
  output out_8,
  output out_9,
  output out_10,
  output out_11,
  output out_12,
  output out_13,
  output out_14
);

  Multiplexer #(.select(2), .width(8)) multiplexer_1 (
    .in0(in_1), .in1(in_2), .in2(in_3), .in3(in_4),
    .out({out_7, out_8, out_9, out_10, out_11, out_12, out_13, out_14}), .sel(in_5), .en(in_6));
endmodule

module \Задание_2  (
  input  [3:0] in_1,
  input  in_2,
  input  [1:0] in_3
);

  wire [3:0] demultiplexer_1_out0, demultiplexer_1_out1, demultiplexer_1_out2, demultiplexer_1_out3;

  Demultiplexer #(.select(2), .width(4)) demultiplexer_1 (
    .out0(demultiplexer_1_out0), .out1(demultiplexer_1_out1), .out2(demultiplexer_1_out2),
    .out3(demultiplexer_1_out3), .in(in_1), .sel(in_3), .en(in_2));
  DotMatrix #(.matrixcols(4), .matrixrows(4)) dotmatrix_1 (
    .col0(demultiplexer_1_out0), .col1(demultiplexer_1_out1), .col2(demultiplexer_1_out2),
    .col3(demultiplexer_1_out3));
endmodule

module \Задание_3  (
  input  in_1,
  input  in_2,
  input  in_3,
  input  in_4,
  input  in_5,
  input  in_6,
  input  in_7,
  input  in_8,
  output out_9
);

  Multiplexer #(.select(3)) multiplexer_1 (
    .in0(in_1), .in1(in_2), .in2(in_3), .in3(in_4), .in4(in_5), .in5(in_6), .in6(in_7), .in7(in_8),
    .out(out_9));  // open: sel, en
endmodule

module \Задание_4  (
  input  in_1,
  input  in_2,
  input  in_3,
  input  in_4,
  input  in_5,
  input  in_6,
  output out_7
);

  wire and_1_out, and_2_out, and_3_out, and_4_out, not_1_out, not_2_out;

  not not_1 (not_1_out, in_5);
  not not_2 (not_2_out, in_6);
  and and_1 (and_1_out, in_1, in_5, in_6);
  and and_2 (and_2_out, in_2, not_1_out, in_6);
  and and_3 (and_3_out, in_3, not_2_out, in_5);
  and and_4 (and_4_out, in_4, not_1_out, not_2_out);
  or or_1 (out_7, and_1_out, and_2_out, and_3_out, and_4_out);
endmodule

module \Задание_5  (
  input  in_1,
  input  in_2,
  input  in_3,
  output out_4,
  output out_5,
  output out_6,
  output out_7
);

  wire not_1_out, not_2_out;

  not not_1 (not_1_out, in_2);
  not not_2 (not_2_out, in_3);
  and and_1 (out_4, in_1, not_2_out, not_1_out);
  and and_2 (out_5, in_1, in_2, not_2_out);
  and and_3 (out_6, in_1, not_1_out, in_3);
  and and_4 (out_7, in_1, in_2, in_3);
endmodule

module \Задание_6  (
  input  in_1,
  input  in_2,
  input  in_3,
  input  in_4,
  input  in_5,
  input  in_6,
  input  in_7,
  input  in_8,
  input  in_9,
  input  in_10,
  input  in_11,
  input  in_12,
  output out_13
);

  wire \задание_4_1_out_7 , \задание_4_2_out_7 ;

  \Задание_4  \u_задание_4_1  (
    .in_1(in_1), .in_2(in_2), .in_3(in_3), .in_4(in_4), .in_5(in_5), .in_6(in_6), .out_7(\задание_4_1_out_7 ));
  \Задание_4  \u_задание_4_2  (
    .in_1(in_7), .in_2(in_8), .in_3(in_9), .in_4(in_10), .in_5(in_11), .in_6(in_12),
    .out_7(\задание_4_2_out_7 ));
  or or_1 (out_13, \задание_4_1_out_7 , \задание_4_2_out_7 );
endmodule
