// Logisim project lr3.circ as structural Verilog: 7 circuits, main circuit 1 Задание
module \_1_Задание  (
  input  in_1,
  input  [7:0] in_2,
  input  [7:0] in_3,
  output [7:0] out_4,
  output out_5
);

  Adder adder_1 (.a(in_2), .b(in_3), .out(out_4), .cin(in_1), .cout(out_5));
endmodule

module \Задание_2  (
  input  A,
  input  B,
  output S,
  output C
);

  wire and_1_out, and_2_out, not_1_out, not_2_out;

  and and_1 (and_1_out, A, not_1_out);
  not not_1 (not_1_out, B);
  not not_2 (not_2_out, A);
  and and_2 (and_2_out, not_2_out, B);
  and and_3 (C, A, B);
  or or_1 (S, and_1_out, and_2_out);
endmodule

module \Задание_3  (
  input  in_1,
  input  in_2,
  input  in_3,
  output out_4,
  output out_5
);

  wire and_1_out, and_2_out, and_3_out, and_4_out, not_1_out, not_2_out, \задание_2_1_s ;

  \Задание_2  \u_задание_2_1  (.A(in_1), .B(in_2), .S(\задание_2_1_s ));  // open: C
  not not_1 (not_1_out, \задание_2_1_s );
  not not_2 (not_2_out, in_3);
  and and_1 (and_1_out, \задание_2_1_s , in_3);
  and and_2 (and_2_out, in_1, in_2);
  and and_3 (and_3_out, in_3, not_1_out);
  and and_4 (and_4_out, not_2_out, \задание_2_1_s );
  or or_1 (out_5, and_1_out, and_2_out);
  or or_2 (out_4, and_3_out, and_4_out);
endmodule

module \Задание_4  (
  input  A7,
  input  B7,
  input  A6,
  input  B6,
  input  A5,
  input  B5,
  input  A4,
  input  B4,
  input  A3,
  input  B3,
  input  A2,
  input  B2,
  input  A1,
  input  B1,
  input  A0,
  input  B0,
  input  Cin,
  output S7,
  output Cout,
  output S6,
  output S5,
  output S4,
  output S3,
  output S2,
  output S1,
  output S0
);

  wire \задание_3_1_out_5 , \задание_3_2_out_5 , \задание_3_3_out_5 , \задание_3_4_out_5 ,
       \задание_3_5_out_5 , \задание_3_6_out_5 , \задание_3_7_out_5 ;

  \Задание_3  \u_задание_3_1  (.in_1(A0), .in_2(B0), .in_3(Cin), .out_4(S0), .out_5(\задание_3_1_out_5 ));
  \Задание_3  \u_задание_3_2  (
    .in_1(A1), .in_2(B1), .in_3(\задание_3_1_out_5 ), .out_4(S1), .out_5(\задание_3_2_out_5 ));
  \Задание_3  \u_задание_3_3  (
    .in_1(A2), .in_2(B2), .in_3(\задание_3_2_out_5 ), .out_4(S2), .out_5(\задание_3_3_out_5 ));
  \Задание_3  \u_задание_3_4  (
    .in_1(A4), .in_2(B4), .in_3(\задание_3_5_out_5 ), .out_4(S4), .out_5(\задание_3_4_out_5 ));
  \Задание_3  \u_задание_3_5  (
    .in_1(A3), .in_2(B3), .in_3(\задание_3_3_out_5 ), .out_4(S3), .out_5(\задание_3_5_out_5 ));
  \Задание_3  \u_задание_3_6  (
    .in_1(A5), .in_2(B5), .in_3(\задание_3_4_out_5 ), .out_4(S5), .out_5(\задание_3_6_out_5 ));
  \Задание_3  \u_задание_3_7  (
    .in_1(A6), .in_2(B6), .in_3(\задание_3_6_out_5 ), .out_4(S6), .out_5(\задание_3_7_out_5 ));
  \Задание_3  \u_задание_3_8  (.in_1(A7), .in_2(B7), .in_3(\задание_3_7_out_5 ), .out_4(S7), .out_5(Cout));
endmodule

module \Задание_5  (
  input  [6:0] in_1
);

  wire button_1_out, comparator_1_eq, comparator_1_gt, comparator_1_lt, or_1_out;
  wire [6:0] keyboard_1_data;

  Keyboard keyboard_1 (.clr(button_1_out), .data(keyboard_1_data));  // open: clk, re, avail
  Button button_1 (.out(button_1_out));
  Comparator #(.width(7)) comparator_1 (
    .a(keyboard_1_data), .b(in_1), .gt(comparator_1_gt), .eq(comparator_1_eq), .lt(comparator_1_lt));
  LED led_1 (.in(comparator_1_eq));
  LED led_2 (.in(or_1_out));
  or or_1 (or_1_out, comparator_1_gt, comparator_1_lt);
endmodule

module \Задание_6  (
  input  a,
  input  b,
  output a_b,
  output a_b_2,
  output a_b_3
);

  wire not_1_out, not_2_out;

  not not_1 (not_1_out, a);
  not not_2 (not_2_out, b);
  and and_1 (a_b, a, not_2_out);
  and and_2 (a_b_3, b, not_1_out);
  nor nor_1 (a_b_2, a_b, a_b_3);
endmodule

module \Задание_7  (
  input  in_1,
  input  in_2,
  input  in_3,
  input  in_4,
  input  in_5,
  input  in_6,
  input  in_7,
  input  in_8,
  input  in_9,
  input  in_10,
  input  in_11,
  input  in_12,
  input  in_13,
  input  in_14,
  input  in_15,
  input  in_16,
  output A_B,
  output A_B_2,
  output A_B_3
);

  wire and_1_out, and_3_out, and_4_out, and_5_out, and_6_out, and_7_out, and_8_out, and_9_out, and_10_out,
       and_11_out, and_12_out, and_13_out, and_14_out, and_15_out, \задание_6_1_a_b , \задание_6_1_a_b_2 ,
       \задание_6_1_a_b_3 , \задание_6_2_a_b , \задание_6_2_a_b_2 , \задание_6_2_a_b_3 , \задание_6_3_a_b ,
       \задание_6_3_a_b_2 , \задание_6_3_a_b_3 , \задание_6_4_a_b , \задание_6_4_a_b_2 , \задание_6_4_a_b_3 ,
       \задание_6_5_a_b , \задание_6_5_a_b_2 , \задание_6_5_a_b_3 , \задание_6_6_a_b , \задание_6_6_a_b_2 ,
       \задание_6_6_a_b_3 , \задание_6_7_a_b , \задание_6_7_a_b_2 , \задание_6_7_a_b_3 , \задание_6_8_a_b ,
       \задание_6_8_a_b_2 , \задание_6_8_a_b_3 ;

  \Задание_6  \u_задание_6_1  (
    .a(in_15), .b(in_16), .a_b(\задание_6_1_a_b ), .a_b_2(\задание_6_1_a_b_2 ), .a_b_3(\задание_6_1_a_b_3 ));
  \Задание_6  \u_задание_6_2  (
    .a(in_13), .b(in_14), .a_b(\задание_6_2_a_b ), .a_b_2(\задание_6_2_a_b_2 ), .a_b_3(\задание_6_2_a_b_3 ));
  \Задание_6  \u_задание_6_3  (
    .a(in_9), .b(in_10), .a_b(\задание_6_3_a_b ), .a_b_2(\задание_6_3_a_b_2 ), .a_b_3(\задание_6_3_a_b_3 ));
  \Задание_6  \u_задание_6_4  (
    .a(in_11), .b(in_12), .a_b(\задание_6_4_a_b ), .a_b_2(\задание_6_4_a_b_2 ), .a_b_3(\задание_6_4_a_b_3 ));
  \Задание_6  \u_задание_6_5  (
    .a(in_7), .b(in_8), .a_b(\задание_6_5_a_b ), .a_b_2(\задание_6_5_a_b_2 ), .a_b_3(\задание_6_5_a_b_3 ));
  \Задание_6  \u_задание_6_6  (
    .a(in_3), .b(in_4), .a_b(\задание_6_6_a_b ), .a_b_2(\задание_6_6_a_b_2 ), .a_b_3(\задание_6_6_a_b_3 ));
  \Задание_6  \u_задание_6_7  (
    .a(in_5), .b(in_6), .a_b(\задание_6_7_a_b ), .a_b_2(\задание_6_7_a_b_2 ), .a_b_3(\задание_6_7_a_b_3 ));
  \Задание_6  \u_задание_6_8  (
    .a(in_1), .b(in_2), .a_b(\задание_6_8_a_b ), .a_b_2(\задание_6_8_a_b_2 ), .a_b_3(\задание_6_8_a_b_3 ));
  and and_1 (and_1_out, \задание_6_6_a_b , \задание_6_8_a_b );
  and and_2 (A_B, \задание_6_8_a_b_2 , \задание_6_6_a_b_2 , \задание_6_7_a_b_2 , \задание_6_5_a_b_2 , \задание_6_3_a_b_2 , \задание_6_4_a_b_2 , \задание_6_2_a_b_2 , \задание_6_1_a_b_2 );
  and and_3 (and_3_out, \задание_6_7_a_b , \задание_6_6_a_b , \задание_6_8_a_b );
  and and_4 (and_4_out, \задание_6_5_a_b , \задание_6_7_a_b , \задание_6_6_a_b , \задание_6_8_a_b );
  or or_1 (A_B_3, and_1_out, and_3_out, and_4_out, and_6_out, and_8_out, and_10_out, and_12_out, \задание_6_8_a_b );
  and and_5 (and_5_out, \задание_6_6_a_b_3 , \задание_6_8_a_b_3 );
  and and_6 (and_6_out, \задание_6_3_a_b , \задание_6_5_a_b , \задание_6_7_a_b , \задание_6_6_a_b , \задание_6_8_a_b );
  and and_7 (and_7_out, \задание_6_7_a_b_3 , \задание_6_6_a_b_3 , \задание_6_8_a_b_3 );
  and and_8 (and_8_out, \задание_6_4_a_b , \задание_6_3_a_b , \задание_6_5_a_b , \задание_6_7_a_b , \задание_6_6_a_b , \задание_6_8_a_b );
  and and_9 (and_9_out, \задание_6_5_a_b_3 , \задание_6_7_a_b_3 , \задание_6_6_a_b_3 , \задание_6_8_a_b_3 );
  and and_10 (and_10_out, \задание_6_2_a_b , \задание_6_4_a_b , \задание_6_3_a_b , \задание_6_5_a_b , \задание_6_7_a_b , \задание_6_6_a_b , \задание_6_8_a_b );
  or or_2 (A_B_2, and_5_out, and_7_out, and_9_out, and_11_out, and_13_out, and_14_out, and_15_out, \задание_6_8_a_b_3 );
  and and_11 (and_11_out, \задание_6_3_a_b_3 , \задание_6_5_a_b_3 , \задание_6_7_a_b_3 , \задание_6_6_a_b_3 , \задание_6_8_a_b_3 );
  and and_12 (and_12_out, \задание_6_1_a_b , \задание_6_2_a_b , \задание_6_4_a_b , \задание_6_3_a_b , \задание_6_5_a_b , \задание_6_7_a_b , \задание_6_6_a_b , \задание_6_8_a_b );
  and and_13 (and_13_out, \задание_6_4_a_b_3 , \задание_6_3_a_b_3 , \задание_6_5_a_b_3 , \задание_6_7_a_b_3 , \задание_6_6_a_b_3 , \задание_6_8_a_b_3 );
  and and_14 (and_14_out, \задание_6_2_a_b_3 , \задание_6_4_a_b_3 , \задание_6_3_a_b_3 , \задание_6_5_a_b_3 , \задание_6_7_a_b_3 , \задание_6_6_a_b_3 , \задание_6_8_a_b_3 );
  and and_15 (and_15_out, \задание_6_1_a_b_3 , \задание_6_2_a_b_3 , \задание_6_4_a_b_3 , \задание_6_3_a_b_3 , \задание_6_5_a_b_3 , \задание_6_7_a_b_3 , \задание_6_6_a_b_3 , \задание_6_8_a_b_3 );
endmodule
