// Logisim project lr4.circ as structural Verilog: 3 circuits, main circuit Задание 1
module \Задание_1  (
  input  \Вход_Set ,
  input  \Вход_синхронизации ,
  input  \Вход_Reset ,
  input  \Вход_принудительной_установки_1 ,
  input  \Вход_принудительного_переброса_значения ,
  input  \Вход_принудительной_установки_0 ,
  output \Выход_Q ,
  output \Выход_Q_обратный 
);

  S_R_Flip_Flop \RS_триггер  (
    .S(\Вход_Set ), .clk(\Вход_синхронизации ), .R(\Вход_Reset ), .Q(\Выход_Q ), .Qn(\Выход_Q_обратный ),
    .preset(\Вход_принудительной_установки_1 ), .reset(\Вход_принудительной_установки_0 ),
    .en(\Вход_принудительного_переброса_значения ));
endmodule

module \Задание_4  (
  input  J,
  input  C,
  input  K,
  input  Q,
  input  minus_Q,
  output Q_2,
  output minus_Q_2
);

  wire and_1_out, and_2_out, clock_1_out, or_1_out, or_2_out;

  Clock clock_1 (.out(clock_1_out));
  and and_1 (and_1_out, J, minus_Q, clock_1_out);
  and and_2 (and_2_out, clock_1_out, Q, K);
  or or_1 (or_1_out, and_1_out, minus_Q);
  or or_2 (or_2_out, Q, and_2_out);
  not not_1 (Q_2, or_1_out);
  not not_2 (minus_Q_2, or_2_out);
endmodule

module \Задание_5  (
);

  wire button_1_out, counter_1_q, even_parity_1_out, odd_parity_1_out;

  Button button_1 (.out(button_1_out));
  Counter #(.width(1), .max('h1)) counter_1 (.Q(counter_1_q));  // open: load, D, count, carry, clk, clr
  buf odd_parity_1 (odd_parity_1_out, counter_1_q);  // Odd_Parity
  not even_parity_1 (even_parity_1_out, counter_1_q);  // Even_Parity
  LED led_1 (.in(odd_parity_1_out));
  LED led_2 (.in(even_parity_1_out));
endmodule
