// Logisim project lr5.circ as structural Verilog: 4 circuits, main circuit main
module main (
  input  [7:0] \Входное_значение ,
  input  \Вкл_Выкл ,
  input  \Вход_синхронизации ,
  input  \Сброс_значения ,
  output [7:0] \Сохраненные_данные 
);

  Register \u_регистр_8_бит  (
    .D(\Входное_значение ), .en(\Вкл_Выкл ), .Q(\Сохраненные_данные ), .clk(\Вход_синхронизации ),
    .clr(\Сброс_значения ));
endmodule

module \Задание_1  (
  input  [7:0] \Входное_значение ,
  input  \Вкл_Выкл ,
  input  \Вход_синхронизации ,
  input  \Сброс_значения ,
  output [7:0] \Сохраненные_данные 
);

  Register \u_регистр_8_бит  (
    .D(\Входное_значение ), .en(\Вкл_Выкл ), .Q(\Сохраненные_данные ), .clk(\Вход_синхронизации ),
    .clr(\Сброс_значения ));
endmodule

module \Задание_2  (
  input  [7:0] in_1,
  input  in_2,
  output [7:0] out_3
);

  and and_1 (out_3[0], in_1[0], in_2);
  and and_2 (out_3[1], in_1[1], in_2);
  and and_3 (out_3[2], in_1[2], in_2);
  and and_4 (out_3[3], in_1[3], in_2);
  and and_5 (out_3[4], in_1[4], in_2);
  and and_6 (out_3[5], in_1[5], in_2);
  and and_7 (out_3[6], in_1[6], in_2);
  and and_8 (out_3[7], in_1[7], in_2);
endmodule

module \Задание_3  (
  input  in_1,
  input  in_2,
  input  in_3,
  input  in_4,
  input  in_5,
  input  in_6,
  input  [1:0] in_7,
  output out_8,
  output out_9,
  output out_10,
  output out_11
);

  wire button_1_out, clock_1_out, multiplexer_1_out, multiplexer_2_out, multiplexer_3_out, multiplexer_4_out,
       undriven, undriven_2;

  Multiplexer #(.select(2)) multiplexer_1 (
    .in0(out_8), .in1(in_1), .in2(undriven), .in3(in_2), .out(multiplexer_1_out), .sel(in_7));  // open: en
  Multiplexer #(.select(2)) multiplexer_2 (
    .in0(undriven), .in1(out_8), .in2(undriven_2), .in3(in_3), .out(multiplexer_2_out), .sel(in_7));  // open: en
  Multiplexer #(.select(2)) multiplexer_3 (
    .in0(undriven_2), .in1(out_8), .in2(out_11), .in3(in_4), .out(multiplexer_3_out), .sel(in_7));  // open: en
  Multiplexer #(.select(2)) multiplexer_4 (
    .in0(out_11), .in1(out_8), .in2(in_5), .in3(in_6), .out(multiplexer_4_out), .sel(in_7));  // open: en
  Clock clock_1 (.out(clock_1_out));
  D_Flip_Flop d_ff_1 (
    .clk(clock_1_out), .D(multiplexer_1_out), .Q(out_8), .reset(button_1_out));  // open: Qn, preset, en
  D_Flip_Flop d_ff_2 (
    .clk(clock_1_out), .D(multiplexer_2_out), .Q(out_8), .reset(button_1_out));  // open: Qn, preset, en
  D_Flip_Flop d_ff_3 (
    .clk(clock_1_out), .D(multiplexer_3_out), .Q(out_8), .reset(button_1_out));  // open: Qn, preset, en
  D_Flip_Flop d_ff_4 (
    .clk(clock_1_out), .D(multiplexer_4_out), .Q(out_11), .reset(button_1_out));  // open: Qn, preset, en
  Button button_1 (.out(button_1_out));

  assign out_9 = out_8;
  assign out_10 = out_8;
endmodule
