// Logisim project lr6.circ as structural Verilog: 8 circuits, main circuit Задание 1
module \Задание_1  (
  input  [7:0] in_1,
  input  in_2,
  input  [7:0] in_3,
  input  in_4,
  input  \обновление ,
  input  \сброс ,
  output out_7
);

  Counter counter_1 (.load(in_2), .D(in_3), .count(in_4), .Q(in_1), .carry(out_7), .clk(\обновление ), .clr(\сброс ));

  // Notes on the sheet:
  //   вкл или изменение режима инкремента
  //   ввод данных
  //   инкремент/декремент
  //   выход из допустиме битов
  //   выход данных
endmodule

module \Задание_2  (
  input  [3:0] in_1,
  input  in_2,
  input  in_3
);

  wire and_1_out, and_2_out, t_ff_1_q;

  T_Flip_Flop t_ff_1 (.clk(in_3), .T(in_2), .Q(t_ff_1_q));  // open: Qn, preset, reset, en
  T_Flip_Flop t_ff_2 (.clk(in_3), .T(in_1[0]), .Q(in_1[1]));  // open: Qn, preset, reset, en
  and and_1 (and_1_out, in_1[0], in_1[1]);
  T_Flip_Flop t_ff_3 (.clk(in_3), .T(and_1_out), .Q(in_1[2]));  // open: Qn, preset, reset, en
  and and_2 (and_2_out, in_1[0], in_1[1], in_1[2]);
  T_Flip_Flop t_ff_4 (.clk(in_3), .T(and_2_out), .Q(in_1[3]));  // open: Qn, preset, reset, en
endmodule

module \Задание_3  (
  input  in_1,
  input  [3:0] in_2,
  input  in_3
);

  wire and_1_out, and_2_out, button_1_out, j_k_ff_1_q, j_k_ff_2_q, j_k_ff_3_q;

  Button button_1 (.out(button_1_out));
  J_K_Flip_Flop j_k_ff_1 (
    .J(in_1), .clk(in_3), .K(in_1), .Q(j_k_ff_1_q), .Qn(in_2[0]), .reset(button_1_out));  // open: preset, en
  J_K_Flip_Flop j_k_ff_2 (
    .J(j_k_ff_1_q), .clk(in_3), .K(j_k_ff_1_q), .Q(j_k_ff_2_q), .Qn(in_2[1]), .reset(button_1_out));  // open: preset, en
  and and_1 (and_1_out, j_k_ff_1_q, j_k_ff_2_q);
  J_K_Flip_Flop j_k_ff_3 (
    .J(and_1_out), .clk(in_3), .K(and_1_out), .Q(j_k_ff_3_q), .Qn(in_2[2]), .reset(button_1_out));  // open: preset, en
  and and_2 (and_2_out, j_k_ff_1_q, j_k_ff_2_q, j_k_ff_3_q);
  J_K_Flip_Flop j_k_ff_4 (
    .J(and_2_out), .clk(in_3), .K(and_2_out), .Qn(in_2[3]), .reset(button_1_out));  // open: Q, preset, en
endmodule

module \Задание_4  (
  input  [3:0] in_1,
  input  in_2,
  input  in_3
);

  wire and_1_out, and_2_out, and_3_out, and_4_out, and_5_out, and_6_out, and_7_out, and_8_out, and_9_out,
       and_10_out, button_1_out, nand_1_out, s_r_ff_1_qn, s_r_ff_2_qn, s_r_ff_3_qn, s_r_ff_4_qn;

  Button button_1 (.out(button_1_out));
  and and_1 (and_1_out, s_r_ff_1_qn, in_2);
  and and_2 (and_2_out, in_2, in_1[0]);
  S_R_Flip_Flop s_r_ff_1 (
    .S(and_1_out), .clk(in_3), .R(and_2_out), .Q(in_1[0]), .Qn(s_r_ff_1_qn), .en(nand_1_out));  // open: preset, reset
  and and_3 (and_3_out, s_r_ff_2_qn, in_1[0]);
  and and_4 (and_4_out, in_1[0], in_1[1]);
  S_R_Flip_Flop s_r_ff_2 (
    .S(and_3_out), .clk(in_3), .R(and_4_out), .Q(in_1[1]), .Qn(s_r_ff_2_qn), .reset(button_1_out),
    .en(nand_1_out));  // open: preset
  and and_5 (and_5_out, in_1[0], in_1[1], in_1[2]);
  and and_6 (and_6_out, in_1[0], in_1[1]);
  and and_7 (and_7_out, s_r_ff_3_qn, and_6_out);
  and and_8 (and_8_out, and_6_out, in_1[2]);
  S_R_Flip_Flop s_r_ff_3 (
    .S(and_7_out), .clk(in_3), .R(and_8_out), .Q(in_1[2]), .Qn(s_r_ff_3_qn), .en(nand_1_out));  // open: preset, reset
  nand nand_1 (nand_1_out, in_1[1], in_1[3]);
  and and_9 (and_9_out, s_r_ff_4_qn, and_5_out);
  and and_10 (and_10_out, and_5_out, in_1[3]);
  S_R_Flip_Flop s_r_ff_4 (
    .S(and_9_out), .clk(in_3), .R(and_10_out), .Q(in_1[3]), .Qn(s_r_ff_4_qn), .reset(button_1_out),
    .en(nand_1_out));  // open: preset
endmodule

module \Компаратор  (
  input  [6:0] in_1,
  input  [6:0] in_2,
  input  in_3,
  output out_4
);

  wire and_1_out, and_2_out, and_3_out, and_4_out, and_5_out, \компаратор_2_1_out_4 , \компаратор_2_2_out_4 ,
       \компаратор_2_3_out_4 , \компаратор_2_4_out_4 , \компаратор_2_5_out_4 , \компаратор_2_6_out_4 ,
       \компаратор_2_7_out_4 ;

  \Компаратор_2  \u_компаратор_2_1  (.in_3(in_3), .out_4(\компаратор_2_1_out_4 ), .in_1(in_1[6]), .in_2(in_2[6]));
  \Компаратор_2  \u_компаратор_2_2  (.in_3(in_3), .out_4(\компаратор_2_2_out_4 ), .in_1(in_1[5]), .in_2(in_2[5]));
  \Компаратор_2  \u_компаратор_2_3  (.in_3(in_3), .out_4(\компаратор_2_3_out_4 ), .in_1(in_1[4]), .in_2(in_2[4]));
  \Компаратор_2  \u_компаратор_2_4  (.in_3(in_3), .out_4(\компаратор_2_4_out_4 ), .in_1(in_1[3]), .in_2(in_2[3]));
  \Компаратор_2  \u_компаратор_2_5  (.in_3(in_3), .out_4(\компаратор_2_5_out_4 ), .in_1(in_1[2]), .in_2(in_2[2]));
  \Компаратор_2  \u_компаратор_2_6  (.in_3(in_3), .out_4(\компаратор_2_6_out_4 ), .in_1(in_1[1]), .in_2(in_2[1]));
  \Компаратор_2  \u_компаратор_2_7  (.in_3(in_3), .out_4(\компаратор_2_7_out_4 ), .in_1(in_1[0]), .in_2(in_2[0]));
  and and_1 (and_1_out, \компаратор_2_1_out_4 , \компаратор_2_2_out_4 );
  and and_2 (and_2_out, and_1_out, \компаратор_2_3_out_4 );
  and and_3 (and_3_out, and_2_out, \компаратор_2_4_out_4 );
  and and_4 (and_4_out, and_3_out, \компаратор_2_5_out_4 );
  and and_5 (and_5_out, and_4_out, \компаратор_2_6_out_4 );
  and and_6 (out_4, and_5_out, \компаратор_2_7_out_4 );
endmodule

module \Компаратор_2  (
  input  in_1,
  input  in_2,
  input  in_3,
  output out_4
);

  wire and_2_out, and_3_out, not_1_out, not_2_out;

  not not_1 (not_1_out, in_2);
  not not_2 (not_2_out, in_1);
  // AND_Gate and_1 has open pins: in0=not_1_out, in1=in_1, out=open
  and and_2 (and_2_out, not_1_out, in_3, not_2_out);
  or or_1 (out_4, and_2_out, and_3_out);
  and and_3 (and_3_out, in_2, in_3, in_1);
  // AND_Gate and_4 has open pins: in0=in_2, in1=not_2_out, out=open
endmodule

module \Задание_5  (
  input  in_1,
  input  [6:0] in_2,
  input  in_3,
  input  [7:0] in_4
);

  wire or_1_out, \компаратор_1_out_4 , \компаратор_2_out_4 , \компаратор_3_out_4 , \компаратор_4_out_4 ,
       \компаратор_5_out_4 , \компаратор_6_out_4 ;

  \Компаратор  \u_компаратор_1  (.in_1(in_2), .in_2(7'b1100101), .in_3(in_3), .out_4(\компаратор_1_out_4 ));
  \Компаратор  \u_компаратор_2  (.in_1(in_2), .in_2(7'b1111001), .in_3(in_3), .out_4(\компаратор_2_out_4 ));
  \Компаратор  \u_компаратор_3  (.in_1(in_2), .in_2(7'b1101001), .in_3(in_3), .out_4(\компаратор_3_out_4 ));
  \Компаратор  \u_компаратор_4  (.in_1(in_2), .in_2(7'b1101111), .in_3(in_3), .out_4(\компаратор_4_out_4 ));
  \Компаратор  \u_компаратор_5  (.in_1(in_2), .in_2(7'b1100001), .in_3(in_3), .out_4(\компаратор_5_out_4 ));
  \Компаратор  \u_компаратор_6  (.in_1(in_2), .in_2(7'b1110101), .in_3(in_3), .out_4(\компаратор_6_out_4 ));
  or or_1 (or_1_out, \компаратор_1_out_4 , \компаратор_2_out_4 , \компаратор_3_out_4 , \компаратор_4_out_4 , \компаратор_5_out_4 , \компаратор_6_out_4 );
  Counter counter_1 (.Q(in_4), .clk(or_1_out), .clr(in_1));  // open: load, D, count, carry
endmodule

module \Задание_5_1  (
);

  wire button_1_out, button_2_out, clock_1_out;
  wire [6:0] keyboard_1_data;
  wire [7:0] undriven;

  Keyboard keyboard_1 (.clk(clock_1_out), .clr(button_1_out), .data(keyboard_1_data));  // open: re, avail
  Button button_1 (.out(button_1_out));
  Clock clock_1 (.out(clock_1_out));
  Button button_2 (.out(button_2_out));
  \Задание_5  \u_задание_5_1  (.in_1(button_2_out), .in_2(keyboard_1_data), .in_3(clock_1_out), .in_4(undriven));
  Hex_Digit_Display hex_digit_display_1 (.value(undriven[7:4]));  // open: dp
  Hex_Digit_Display hex_digit_display_2 (.value(undriven[3:0]));  // open: dp
endmodule
