// Logisim project lr7.circ as structural Verilog: 4 circuits, main circuit Зд 1
module \Зд_1  (
  input  a,
  input  b,
  input  p,
  input  [1:0] a_2,
  output q,
  output P_2
);

  wire adder_1_out, and_1_out, not_1_out, or_1_out;

  not not_1 (not_1_out, a);
  or or_1 (or_1_out, a, b);
  and and_1 (and_1_out, a, b);
  Adder #(.width(1)) adder_1 (.a(a), .b(b), .out(adder_1_out), .cin(p), .cout(P_2));
  Multiplexer #(.select(2), .enable("false")) multiplexer_1 (
    .in0(not_1_out), .in1(or_1_out), .in2(and_1_out), .in3(adder_1_out), .out(q), .sel(a_2));
endmodule

module _2 (
  input  a0,
  input  a1,
  input  a2,
  input  a3,
  input  b0,
  input  b1,
  input  b2,
  input  b3,
  input  p,
  input  [1:0] s,
  output [3:0] out_11,
  output P_2
);

  wire \зд_1_1_p_2 , \зд_1_2_p_2 , \зд_1_3_p_2 ;

  \Зд_1  \u_зд_1_1  (.q(out_11[0]), .P_2(\зд_1_1_p_2 ), .a(a0), .b(b0), .p(p), .a_2(s));
  \Зд_1  \u_зд_1_2  (.q(out_11[1]), .P_2(\зд_1_2_p_2 ), .a(a1), .b(b1), .p(\зд_1_1_p_2 ), .a_2(s));
  \Зд_1  \u_зд_1_3  (.q(out_11[2]), .P_2(\зд_1_3_p_2 ), .a(a2), .b(b2), .p(\зд_1_2_p_2 ), .a_2(s));
  \Зд_1  \u_зд_1_4  (.q(out_11[3]), .P_2(P_2), .a(a3), .b(b3), .p(\зд_1_3_p_2 ), .a_2(s));
endmodule

module \Зд_3_и_4  (
  input  [7:0] in_1,
  input  [7:0] in_2,
  input  [3:0] in_3,
  input  in_4,
  input  in_5,
  output [7:0] out_6,
  output [7:0] out_7
);

  \_8_битное_АЛУ  \u_8_битное_алу_1  (
    .out_11(out_6), .P_2(out_7[0]), .a(in_1), .b(in_2), .p(in_5), .m(in_4), .s(in_3), .NF(out_7[1]),
    .GNF(out_7[2]), .ON(out_7[3]), .EN(out_7[4]), .AO(out_7[5]), .LO(out_7[6]), .AF(out_7[7]));
  LED overflow (.in(out_7[0]));
  LED _0_flag (.in(out_7[1]));
  LED _0_flag_2 (.in(out_7[2]));
  LED odd_number (.in(out_7[3]));
  LED even_number (.in(out_7[4]));
  LED arithmetic_operation (.in(out_7[5]));
  LED logical_operation (.in(out_7[6]));
  LED alternating_number (.in(out_7[7]));
endmodule

module \_8_битное_АЛУ  (
  input  [7:0] a,
  input  [7:0] b,
  input  p,
  input  m,
  input  [3:0] s,
  output GNF,
  output NF,
  output ON,
  output EN,
  output P_2,
  output [7:0] out_11,
  output AO,
  output LO,
  output AF
);

  wire adder_1_cout, adder_2_cout, and_2_out, and_3_out, comparator_1_gt, comparator_1_lt, comparator_2_eq,
       comparator_3_eq;
  wire [7:0] _1, _4, _6, _9, adder_1_out, adder_2_out, B_t, C, E, F, not_3_out, not_4_out, RX,
       subtractor_1_out, subtractor_2_out, X;

  Comparator comparator_1 (.a({out_11[7:1], ON}), .b({8{1'b0}}), .gt(comparator_1_gt), .eq(NF), .lt(comparator_1_lt));
  or or_1 (GNF, comparator_1_lt, comparator_1_gt);
  not not_1 (EN, ON);
  not not_2 (AO, m);
  Comparator comparator_2 (.a({out_11[7:1], ON}), .b(8'h55), .eq(comparator_2_eq));  // open: gt, lt
  Comparator comparator_3 (.a({out_11[7:1], ON}), .b(8'haa), .eq(comparator_3_eq));  // open: gt, lt
  assign not_3_out = ~a;  // NOT_Gate not_3, 8 bits wide
  or or_2 (AF, comparator_2_eq, comparator_3_eq);
  assign not_4_out = ~b;  // NOT_Gate not_4, 8 bits wide
  Multiplexer #(.select(4), .width(8), .enable("false")) multiplexer_1 (
    .in0(not_3_out), .in1(_1), .in2({8{1'b0}}), .in3({8{1'b0}}), .in4(_4), .in5(not_4_out), .in6(_6),
    .in7({8{1'b0}}), .in8({8{1'b0}}), .in9(_9), .in10(b), .in11(B_t), .in12(C), .in13({8{1'b0}}), .in14(E),
    .in15(F), .out({out_11[7:1], ON}), .sel(s));
  Subtractor subtractor_1 (.a(a), .b(8'h1), .out(subtractor_1_out));  // open: bin, bout
  Multiplexer #(.width(8), .enable("false")) multiplexer_2 (.in0(subtractor_1_out), .in1(a), .out(F), .sel(m));
  assign E = a | b;  // OR_Gate or_3, 8 bits wide
  assign _1 = ~E;  // NOT_Gate not_5, 8 bits wide
  assign B_t = a & b;  // AND_Gate and_1, 8 bits wide
  assign _4 = ~B_t;  // NOT_Gate not_6, 8 bits wide
  assign X = a ^ b;  // XOR_Gate xor_1, 8 bits wide
  assign RX = ~X;  // NOT_Gate not_7, 8 bits wide
  Adder adder_1 (.a(a), .b(b), .out(adder_1_out), .cin(p), .cout(adder_1_cout));
  Subtractor subtractor_2 (.a(a), .b(b), .out(subtractor_2_out));  // open: bin, bout
  Adder adder_2 (.a(a), .b(a), .out(adder_2_out), .cin(p), .cout(adder_2_cout));
  Multiplexer #(.width(8), .enable("false")) multiplexer_3 (.in0(adder_1_out), .in1(RX), .out(_9), .sel(m));
  Multiplexer #(.width(8), .enable("false")) multiplexer_4 (.in0(subtractor_2_out), .in1(X), .out(_6), .sel(m));
  Multiplexer #(.width(8), .enable("false")) multiplexer_5 (.in0(adder_2_out), .in1(8'hf), .out(C), .sel(m));
  and and_2 (and_2_out, adder_1_cout, ~m);  // AND_Gate
  and and_3 (and_3_out, adder_2_cout, ~m);  // AND_Gate
  Multiplexer #(.select(4), .enable("false")) multiplexer_6 (
    .in0(1'b0), .in1(1'b0), .in2(1'b0), .in3(1'b0), .in4(1'b0), .in5(1'b0), .in6(1'b0), .in7(1'b0),
    .in8(1'b0), .in9(and_2_out), .in10(1'b0), .in11(1'b0), .in12(and_3_out), .in13(1'b0), .in14(1'b0),
    .in15(1'b0), .out(P_2), .sel(s));

  assign LO = m;
  assign out_11[0] = ON;

  // Other names for the same wires on the sheet: out[7:0] = {out_11[7:1], ON}; ss[3:0] = s
endmodule
