// Logisim project lr8.circ as structural Verilog: 5 circuits, main circuit Задание 1
module \Задание_1  (
  input  [3:0] \Указывает_адрес_ячейки_памяти ,
  input  \активирует_или_деактивирует_работу_ОЗУ ,
  input  \синхронизация_операций_ОЗУ ,
  input  \управляет_режимом_работы_ОЗУ ,
  input  \сброс_содержимого_всей_памяти ,
  output [3:0] \Выход_для_передачи_данных 
);

  RAM #(.addrWidth(4), .dataWidth(4)) ram_1 (
    .addr(\Указывает_адрес_ячейки_памяти ), .data(\Выход_для_передачи_данных ),
    .sel(\активирует_или_деактивирует_работу_ОЗУ ), .clk(\синхронизация_операций_ОЗУ ),
    .ld(\управляет_режимом_работы_ОЗУ ), .clr(\сброс_содержимого_всей_памяти ));
endmodule

module \Задание_2  (
  input  [3:0] \указывает__какую_ячейку_памяти_нужно_выбрать ,
  input  \сигнал_разрешения ,
  output [3:0] \данные__хранящиеся_по_адресу__указанному_на_входе_A 
);

  ROM #(.addrWidth(4), .dataWidth(4)) rom_1 (
    .addr(\указывает__какую_ячейку_памяти_нужно_выбрать ),
    .data(\данные__хранящиеся_по_адресу__указанному_на_входе_A ), .sel(\сигнал_разрешения ));
endmodule

module \Задание_3  (
  input  [7:0] in_1,
  input  [7:0] in_2,
  input  [7:0] in_3,
  input  [7:0] in_4,
  input  [7:0] in_5,
  input  [7:0] in_6,
  input  [7:0] in_7,
  input  [7:0] in_8,
  input  [7:0] in_9,
  input  [7:0] in_10,
  input  [7:0] in_11,
  input  [7:0] in_12,
  input  [7:0] in_13,
  input  [7:0] in_14,
  input  [7:0] in_15,
  input  [7:0] in_16,
  output [7:0] out_17,
  output [7:0] out_18,
  output [7:0] out_19,
  output [7:0] out_20,
  output [7:0] out_21,
  output [7:0] out_22,
  output [7:0] out_23,
  output [7:0] out_24
);

  // AND_Gate and_1 is placed but not wired
  // AND_Gate and_2 is placed but not wired
  // AND_Gate and_3 is placed but not wired
  // AND_Gate and_4 is placed but not wired
  // AND_Gate and_5 is placed but not wired
  // AND_Gate and_6 is placed but not wired
  // AND_Gate and_7 is placed but not wired
  // AND_Gate and_8 is placed but not wired
  // AND_Gate and_9 is placed but not wired
  // AND_Gate and_10 is placed but not wired
  // AND_Gate and_11 is placed but not wired
  // AND_Gate and_12 is placed but not wired
  // AND_Gate and_13 is placed but not wired
  // AND_Gate and_14 is placed but not wired
  // AND_Gate and_15 is placed but not wired
  // AND_Gate and_16 is placed but not wired
  Decoder #(.select(4)) decoder_1 ();  // open: out0, out1, out2, out3, out4, out5, out6, out7, out8, out9, out10, out11, out12, out13, out14, out15, sel, en
  Multiplexer #(.select(4), .width(8)) multiplexer_1 ();  // open: in0, in1, in2, in3, in4, in5, in6, in7, in8, in9, in10, in11, in12, in13, in14, in15, out, sel, en
endmodule

module \Задание_4  (
  input  in_1
);

  wire clock_1_out;
  wire [6:0] ram_1_data;
  wire [7:0] counter_1_q;

  Clock clock_1 (.out(clock_1_out));
  Counter counter_1 (.Q(counter_1_q), .clk(clock_1_out));  // open: load, D, count, carry, clr
  RAM #(.dataWidth(7)) ram_1 (.addr(counter_1_q), .data(ram_1_data), .clk(clock_1_out));  // open: sel, ld, clr
  TTY tty_1 (.data(ram_1_data), .clk(clock_1_out), .we(clock_1_out), .clr(in_1));
endmodule

module \Задание_5  (
);

  Keyboard keyboard_1 ();  // open: clk, re, clr, avail, data
  Button button_1 ();  // open: out
  Clock clock_1 ();  // open: out
  TTY tty_1 ();  // open: data, clk, we, clr
endmodule
